// Logisim project Root.circ as structural Verilog: 5 circuits, main circuit main
module main (
  input  [16:0] in_1,
  output [16:0] out_2
);

  wire clock_1_out, controlblock_1_mux, controlblock_1_ready, controlblock_1_wrcount, controlblock_1_wrln,
       controlblock_1_wrsquare, datapath_1_comp_saida, datapath_1_zeroorless, Rst_out;

  Button Rst (.out(Rst_out));
  Clock clock_1 (.out(clock_1_out));
  LED Ready (.in(controlblock_1_ready));
  ControlBlock controlblock_1 (
    .Zero(datapath_1_zeroorless), .Rst(Rst_out), .Comp(datapath_1_comp_saida), .Clk(clock_1_out),
    .wrCount(controlblock_1_wrcount), .wrSquare(controlblock_1_wrsquare), .wrln(controlblock_1_wrln),
    .Ready(controlblock_1_ready), .Mux(controlblock_1_mux));
  DataPath datapath_1 (
    .in_1(in_1), .wrSquare_Entrada(controlblock_1_wrsquare), .wrCount_Entrada(controlblock_1_wrcount),
    .wrln_Entrada(controlblock_1_wrln), .Mux_Entrada(controlblock_1_mux), .Comp_Saida(datapath_1_comp_saida),
    .ZeroOrLess(datapath_1_zeroorless), .Saida(out_2), .Rst_Entrada(Rst_out));
endmodule

module NextState (
  input  Q1,
  input  Q0,
  input  Zero,
  input  Reset,
  input  Comp,
  output S1,
  output S2
);

  wire and_1_out, and_2_out, and_3_out, and_4_out, and_5_out, and_6_out, not_1_out, not_2_out, not_3_out,
       not_4_out, not_5_out, not_6_out, not_7_out, not_8_out, not_9_out;

  not not_1 (not_1_out, Q0);
  not not_2 (not_2_out, Reset);
  not not_3 (not_3_out, Comp);
  not not_4 (not_4_out, Q0);
  not not_5 (not_5_out, Reset);
  not not_6 (not_6_out, Q1);
  not not_7 (not_7_out, Reset);
  not not_8 (not_8_out, Reset);
  not not_9 (not_9_out, Q0);
  and and_1 (and_1_out, not_1_out, not_2_out, not_3_out);
  and and_2 (and_2_out, Q1, not_4_out);
  and and_3 (and_3_out, Q1, not_5_out);
  and and_4 (and_4_out, not_6_out, not_7_out, Comp);
  and and_5 (and_5_out, Q0, not_8_out);
  and and_6 (and_6_out, Q1, not_9_out, Zero);
  or or_1 (S1, and_1_out, and_2_out, and_3_out);
  or or_2 (S2, and_4_out, and_5_out, and_6_out);
endmodule

module \saídas  (
  input  Q1,
  input  Q0,
  output wrCount,
  output wrSquare,
  output wrIn,
  output Ready,
  output Mux
);

  wire not_5_out;

  not not_1 (wrCount, Q0);
  not not_2 (wrSquare, Q0);
  not not_3 (wrIn, Q0);
  not not_4 (Ready, Q0);
  not not_5 (not_5_out, Q0);
  and and_1 (Mux, Q1, not_5_out);
endmodule

module DataPath (
  input  [16:0] in_1,
  input  Rst_Entrada,
  input  wrSquare_Entrada,
  input  wrCount_Entrada,
  input  wrln_Entrada,
  input  Mux_Entrada,
  output Comp_Saida,
  output ZeroOrLess,
  output [16:0] Saida
);

  wire clock_1_out, nor_1_out;
  wire [16:0] adder_1_out, adder_2_out, Input_q, multiplexer_1_out, multiplexer_2_out, multiplexer_3_out,
       Square_q, subtractor_1_out;

  Comparator #(.width(17)) comparator_1 (.a({17{1'b0}}), .b(in_1), .eq(Comp_Saida));  // open: gt, lt
  Multiplexer #(.width(17)) multiplexer_1 (
    .in0(in_1), .in1(subtractor_1_out), .out(multiplexer_1_out), .sel(Mux_Entrada));  // open: en
  Multiplexer #(.width(17)) multiplexer_2 (
    .in0(17'h1), .in1(adder_2_out), .out(multiplexer_2_out), .sel(Mux_Entrada));  // open: en
  Multiplexer #(.width(17)) multiplexer_3 (
    .in0({17{1'b0}}), .in1(adder_1_out), .out(multiplexer_3_out), .sel(Mux_Entrada));  // open: en
  Clock clock_1 (.out(clock_1_out));
  Register #(.width(17)) Input (
    .D(multiplexer_1_out), .en(wrln_Entrada), .Q(Input_q), .clk(clock_1_out), .clr(Rst_Entrada));
  Register #(.width(17)) Square (
    .D(multiplexer_2_out), .en(wrSquare_Entrada), .Q(Square_q), .clk(clock_1_out), .clr(Rst_Entrada));
  Register #(.width(17)) Count (
    .D(multiplexer_3_out), .en(wrCount_Entrada), .Q(Saida), .clk(clock_1_out), .clr(Rst_Entrada));
  Adder #(.width(17)) adder_1 (.a(Saida), .b(17'h1), .out(adder_1_out));  // open: cin, cout
  Subtractor #(.width(17)) subtractor_1 (.a(Input_q), .b(Square_q), .out(subtractor_1_out));  // open: bin, bout
  Adder #(.width(17)) adder_2 (.a(Square_q), .b(17'h2), .out(adder_2_out));  // open: cin, cout
  nor nor_1 (nor_1_out, Input_q[0], Input_q[1], Input_q[2], Input_q[3], Input_q[4], Input_q[5], Input_q[6], Input_q[7], Input_q[8], Input_q[9], Input_q[10], Input_q[11], Input_q[12], Input_q[13], Input_q[14], Input_q[15], Input_q[16]);
  or or_1 (ZeroOrLess, nor_1_out, Input_q[16]);

  // Other names for the same wires on the sheet: Mux = Mux_Entrada; Rst = Rst_Entrada; wrCount = wrCount_Entrada;
  //   wrIn = wrln_Entrada; wrSquare = wrSquare_Entrada
endmodule

module ControlBlock (
  input  Zero,
  input  Rst,
  input  Comp,
  input  Clk,
  output wrCount,
  output wrSquare,
  output wrln,
  output Ready,
  output Mux
);

  wire and_1_out, \saídas_1_wrcount ;
  wire [1:0] nextstate_1_s2, register_1_q;

  NextState nextstate_1 (
    .Q1(register_1_q[1]), .Q0(register_1_q[0]), .Zero(Zero), .Reset(Rst), .Comp(Comp),
    .S1(nextstate_1_s2[1]), .S2(nextstate_1_s2[0]));
  Register #(.width(2)) register_1 (.D(nextstate_1_s2), .Q(register_1_q), .clk(Clk));  // open: en, clr
  and and_1 (and_1_out, nextstate_1_s2[0], nextstate_1_s2[1]);
  \saídas  \saídas_1  (
    .Q1(register_1_q[1]), .Q0(register_1_q[0]), .wrCount(\saídas_1_wrcount ), .wrSquare(wrSquare),
    .wrIn(wrln), .Ready(Ready), .Mux(Mux));
  and and_2 (wrCount, ~and_1_out, \saídas_1_wrcount );  // AND_Gate
endmodule
